# Fritzing sketch I-Swipe Schematics (saved by Fritzing 0.9.3b)
breadboards: 1

parts:
  HC-SR04_Sensor_1 = HC-SR04 Ultrasonic Distance Sensor
  HC-SR04_Sensor_2 = HC-SR04 Ultrasonic Distance Sensor
  Part1 = Arduino Uno (Rev3) - ICSP
  LED1 = LED - 3mm [color="Red (633nm)" package="3 mm [THT]"]
  LED2 = LED - 3mm [color="Red (633nm)" package="3 mm [THT]"]
  R1 = Resistor [tolerance=±5% resistance=220 package="2010 [SMD]"]
  R2 = Resistor [tolerance=±5% resistance=220 package="2010 [SMD]"]

nets:
  VCC: HC-SR04_Sensor_1.VCC, HC-SR04_Sensor_2.VCC, Part1.5V
  N1: HC-SR04_Sensor_1.TRIG, Part1.D3_PWM
  N2: HC-SR04_Sensor_1.ECHO, Part1.D2
  GND: HC-SR04_Sensor_1.GND, HC-SR04_Sensor_2.GND, Part1.GND, LED1.cathode, LED2.cathode
  N3: HC-SR04_Sensor_2.TRIG, Part1.D5_PWM
  N4: HC-SR04_Sensor_2.ECHO, Part1.D4
  N5: Part1.D6_PWM, R2.Pin_1
  N6: Part1.D7, R1.Pin_1
  N7: LED1.anode, R1.Pin_0
  N8: LED2.anode, R2.Pin_0
